// Logisim project example_NOD (with_filter).circ as structural Verilog: 4 circuits, main circuit main
module main (
  input  [7:0] in_1,
  output [7:0] out_2,
  output [1:0] out_3
);

  wire button_1_out, button_2_out, clock_1_out, filter_1_out_5, oa_1_p0, oa_1_p1, oa_1_p2, oa_1_p3, oa_1_ro;
  wire [11:0] ya_1_out_8;

  Clock clock_1 (.out(clock_1_out));
  Button button_1 (.out(button_1_out));
  Button button_2 (.out(button_2_out));
  // Probe on in_1
  OA oa_1 (
    .in_1(clock_1_out), .INPUT(in_1), .in_3(ya_1_out_8), .OUTPUT(out_2), .p3(oa_1_p3), .p2(oa_1_p2),
    .p0(oa_1_p0), .p1(oa_1_p1), .out_8(out_3), .RO(oa_1_ro));
  filter filter_1 (.in_1(clock_1_out), .in_2(button_1_out), .in_3(1'b1), .out_5(filter_1_out_5));  // open: out_4
  // Probe on out_2
  LED led_1 (.in(oa_1_ro));
  YA ya_1 (
    .RI(filter_1_out_5), .p0(oa_1_p0), .p1(oa_1_p1), .p2(oa_1_p2), .p3(oa_1_p3), .Ready_RST(button_2_out),
    .in_7(clock_1_out), .out_8(ya_1_out_8));

  // Notes on the sheet:
  //   RI
  //   Ready_RST
  //   НОД двух положительных чисел в дополнительном коде
  //   Рекомендуемая тактовая частота: >=1 кГц
  //   ERROR CODES:
  //   00 - нет ошибки
  //   01 - один или оба операнда отрицательные
  //   10 - один или оба операнда равны нулю
endmodule

module YA (
  input  RI,
  input  p0,
  input  p1,
  input  p2,
  input  p3,
  input  Ready_RST,
  input  in_7,
  output [11:0] out_8
);

  wire [0:0] multiplexer_1_out;
  wire [3:0] H, register_1_q, rom_1_data;

  Multiplexer #(.select(4)) multiplexer_1 (
    .in0(RI), .in1(p0), .in2(p1), .in3(p2), .in4(p3), .in5(Ready_RST), .out(multiplexer_1_out[0]), .sel(H));  // open: in6, in7, in8, in9, in10, in11, in12, in13, in14, in15, en
  ROM #(.addrWidth(5), .dataWidth(4)) rom_1 (
    .addr({register_1_q, multiplexer_1_out[0]}), .data(rom_1_data));  // open: sel
  Register #(.width(4)) register_1 (.D(rom_1_data), .Q(register_1_q), .clk(in_7));  // open: en, clr
  ROM #(.addrWidth(4), .dataWidth(16)) rom_2 (.addr(register_1_q), .data({out_8, H}));  // open: sel

  // Notes on the sheet:
  //   contents of rom_1 (hex, n*v repeats v):
  //   8 1 9 2 a 3 d 0 d 0 d 0 c 5 c 5 8 1 9 2 b 4 c 5 7 6 d
  //   contents of rom_2 (hex, n*v repeats v):
  //   8000 1000 801 165 1a5 135 5203 2c03 0 0 2 3 4 15
endmodule

module OA (
  input  in_1,
  input  [7:0] INPUT,
  input  [11:0] in_3,
  output [7:0] OUTPUT,
  output p3,
  output p2,
  output p0,
  output [1:0] out_8,
  output p1,
  output RO
);

  wire A7, AOR, B7, BOR;
  wire [6:0] register_1_q, register_2_q;
  wire [7:0] multiplexer_1_out, multiplexer_2_out, multiplexer_3_out, multiplexer_4_out, not_1_out,
       not_2_out, SM;

  or or_1 (p0, A7, B7);
  Multiplexer #(.width(8)) multiplexer_1 (.in0(INPUT), .in1(SM), .out(multiplexer_1_out), .sel(in_3[10]));  // open: en
  Multiplexer #(.width(8)) multiplexer_2 (.in0(INPUT), .in1(SM), .out(multiplexer_2_out), .sel(in_3[9]));  // open: en
  nand nand_1 (p1, AOR, BOR);
  Register register_1 (.D(multiplexer_1_out), .en(in_3[8]), .Q({A7, register_1_q}), .clk(in_1), .clr(in_3[11]));
  Register register_2 (.D(multiplexer_2_out), .en(in_3[7]), .Q({B7, register_2_q}), .clk(in_1), .clr(in_3[11]));
  Comparator comparator_1 (.a({A7, register_1_q}), .b({B7, register_2_q}), .gt(p3), .eq(p2));  // open: lt
  or or_2 (AOR, register_1_q[0], register_1_q[1], register_1_q[2], register_1_q[3], register_1_q[4], register_1_q[5], register_1_q[6], A7);
  or or_3 (BOR, register_2_q[0], register_2_q[1], register_2_q[2], register_2_q[3], register_2_q[4], register_2_q[5], register_2_q[6], B7);
  Register #(.width(2)) register_3 (.D(in_3[3:2]), .en(in_3[4]), .Q(out_8), .clk(in_1), .clr(in_3[11]));
  D_Flip_Flop d_ff_1 (.clk(in_1), .D(1'b1), .Q(RO), .en(in_3[1]), .reset(in_3[11]));  // open: Qn, preset
  assign OUTPUT = in_3[0] ? {A7, register_1_q} : 8'bz;  // Controlled_Buffer controlled_buffer_1
  assign not_1_out = ~{A7, register_1_q};  // NOT_Gate not_1, 8 bits wide
  assign not_2_out = ~{B7, register_2_q};  // NOT_Gate not_2, 8 bits wide
  Multiplexer #(.width(8)) multiplexer_3 (
    .in0({A7, register_1_q}), .in1(not_1_out), .out(multiplexer_3_out), .sel(in_3[6]));  // open: en
  Multiplexer #(.width(8)) multiplexer_4 (
    .in0({B7, register_2_q}), .in1(not_2_out), .out(multiplexer_4_out), .sel(in_3[5]));  // open: en
  Adder adder_1 (.a(multiplexer_3_out), .b(multiplexer_4_out), .out(SM), .cin(1'b1));  // open: cout

  // Other names for the same wires on the sheet: CLK = in_1; LBUF = in_3[0]; LRO = in_3[1]; DER[1:0] = in_3[3:2];
  //   LER = in_3[4]; INVB = in_3[5]; INVA = in_3[6]; LRGB = in_3[7]; LRGA = in_3[8]; MXB = in_3[9]; MXA = in_3[10];
  //   RST = in_3[11]

  // Notes on the sheet:
  //   RG_A
  //   RG_B
  //   RG_ER
endmodule

module filter (
  input  in_1,
  input  in_2,
  input  in_3,
  output out_4,
  output out_5
);

  wire and_1_out, and_2_out, and_3_out, d_ff_1_q, d_ff_2_q, d_ff_3_q, xnor_1_out;
  wire [3:0] counter_1_q;

  Counter #(.width(4), .max('hf)) counter_1 (
    .count(in_3), .Q(counter_1_q), .clk(in_1), .clr(xnor_1_out));  // open: load, D, carry
  D_Flip_Flop d_ff_1 (.clk(in_1), .D(in_2), .Q(d_ff_1_q));  // open: Qn, preset, en, reset
  D_Flip_Flop d_ff_2 (.clk(in_1), .D(d_ff_1_q), .Q(d_ff_2_q));  // open: Qn, preset, en, reset
  and and_1 (and_1_out, counter_1_q[0], counter_1_q[1], counter_1_q[2], counter_1_q[3]);
  and and_2 (and_2_out, and_1_out, in_3);
  D_Flip_Flop d_ff_3 (.clk(in_1), .D(d_ff_2_q), .Q(d_ff_3_q), .en(and_2_out));  // open: Qn, preset, reset
  and and_3 (and_3_out, d_ff_2_q, and_2_out);
  buf buffer_1 (out_4, d_ff_3_q);
  xnor xnor_1 (xnor_1_out, d_ff_3_q, d_ff_2_q);
  D_Flip_Flop d_ff_4 (.clk(in_1), .D(and_3_out), .Q(out_5));  // open: Qn, preset, en, reset

  // Other names for the same wires on the sheet: CLK = in_1
endmodule
