// Logisim project pr3.circ as structural Verilog
module \ВУ_миста_майк_вазовский  (
  input  [7:0] in_1,
  output [7:0] out_2,
  output [1:0] out_3,
  output out_4
);

  wire button_1_out, button_2_out, CLK, \oa_майк_вазовский_1_out_7 , \oa_майк_вазовский_1_out_8 , RI, RST;
  wire [7:0] \уа_с_2_адресами_в_памяти_1_out_6 ;

  Button button_1 (.out(button_1_out));
  Button button_2 (.out(button_2_out));
  \OA_майк_вазовский  \oa_майк_вазовский_1  (
    .in_1(in_1), .in_2(\уа_с_2_адресами_в_памяти_1_out_6 ), .in_3(CLK), .out_4(out_2), .out_5(out_3),
    .out_7(\oa_майк_вазовский_1_out_7 ), .out_8(\oa_майк_вазовский_1_out_8 ), .out_6(out_4));
  filter filter_1 (.in_1(CLK), .in_2(button_1_out), .in_3(1'b1), .out_5(RI));  // open: out_4
  filter filter_2 (.in_1(CLK), .in_2(button_2_out), .in_3(1'b1), .out_5(RST));  // open: out_4
  Clock clock_1 (.out(CLK));
  \УА_с_2_адресами_в_памяти  \u_уа_с_2_адресами_в_памяти_1  (
    .in_1(RI), .in_2(\oa_майк_вазовский_1_out_7 ), .in_3(\oa_майк_вазовский_1_out_8 ), .in_4(RST),
    .in_5(CLK), .out_6(\уа_с_2_адресами_в_памяти_1_out_6 ));

  // Other names for the same wires on the sheet: D[7:0] = out_2; ER[1:0] = out_3; IN[7:0] = in_1; RO = out_4
endmodule

module \OA_майк_вазовский  (
  input  [7:0] in_1,
  input  [7:0] in_2,
  input  in_3,
  output [7:0] out_4,
  output [1:0] out_5,
  output out_6,
  output out_7,
  output out_8
);

  wire nand_1_out, or_1_out, or_2_out, or_4_out;
  wire [7:0] RG_A, RG_B, RG_C;

  Register register_1 (.D(in_1), .en(in_2[6]), .Q(RG_A), .clk(in_3), .clr(in_2[7]));
  Register register_2 (.D(in_1), .en(in_2[5]), .Q(RG_B), .clk(in_3), .clr(in_2[7]));
  Register register_3 (.D(out_4), .en(in_2[4]), .Q(RG_C), .clk(in_3), .clr(in_2[7]));
  Adder adder_1 (.a(RG_A), .b(RG_B), .out(out_4));  // open: cin, cout
  Register #(.width(2)) register_4 (.D(in_2[2:1]), .en(in_2[3]), .Q(out_5), .clk(in_3), .clr(in_2[7]));
  D_Flip_Flop d_ff_1 (.clk(in_3), .D(1'b1), .Q(out_6), .en(in_2[0]), .reset(in_2[7]));  // open: Qn, preset
  or or_1 (or_1_out, RG_A[0], RG_A[1], RG_A[2], RG_A[3], RG_A[4], RG_A[5], RG_A[6], RG_A[7]);
  or or_2 (or_2_out, RG_B[0], RG_B[1], RG_B[2], RG_B[3], RG_B[4], RG_B[5], RG_B[6], RG_B[7]);
  nand nand_1 (nand_1_out, or_1_out, or_2_out);
  and and_1 (out_8, RG_C[7], ~RG_A[7], ~RG_B[7]);  // AND_Gate
  or or_3 (out_7, nand_1_out, or_4_out);
  or or_4 (or_4_out, RG_A[7], RG_B[7]);

  // Other names for the same wires on the sheet: CLK = in_3; CMD[7:0] = in_2; LRO = in_2[0]; DER[1:0] = in_2[2:1];
  //   LER = in_2[3]; LRG_C = in_2[4]; LRG_B = in_2[5]; LRG_A = in_2[6]; RST = in_2[7]; D[7:0] = out_4;
  //   ER[1:0] = out_5; IN[7:0] = in_1; P0 = out_7; P1 = out_8; RG_A_7 = RG_A[7]; RG_B_7 = RG_B[7]; RG_C_7 = RG_C[7];
  //   RG_RO = out_6

  // Notes on the sheet:
  //   INPUT
  //   RAM
  //   KC
  //   P0
  //   P1
  //   OUTPUT
endmodule

module \УА_с_2_адресами_в_памяти  (
  input  in_1,
  input  in_2,
  input  in_3,
  input  in_4,
  input  in_5,
  output [7:0] out_6
);

  wire multiplexer_1_out;
  wire [3:0] A0, A1, H, multiplexer_2_out, register_1_q;

  Multiplexer #(.select(2), .disabled(0), .enable("false")) multiplexer_1 (
    .in0(in_1), .in1(in_2), .in2(in_3), .in3(in_4), .out(multiplexer_1_out), .sel(H[1:0]));
  Multiplexer #(.width(4), .disabled(0), .enable("false")) multiplexer_2 (
    .in0(A0), .in1(A1), .out(multiplexer_2_out), .sel(multiplexer_1_out));
  Register #(.width(4)) register_1 (.D(multiplexer_2_out), .Q(register_1_q), .clk(in_5));  // open: en, clr
  ROM #(.addrWidth(4), .dataWidth(20)) rom_1 (.addr(register_1_q), .data({out_6, H, A0, A1}));  // open: sel

  // Other names for the same wires on the sheet: CMD[7:0] = out_6; CLK = in_5; P0 = in_2; P1 = in_3; RI = in_1;
  //   RST = in_4

  // Notes on the sheet:
  //   contents of rom_1 (hex, n*v repeats v):
  //   80071 40082 200aa b390 100bb d390 9390 71 82 390 143 265
endmodule

module \УА_c_регулярной_адресацией  (
  input  in_1,
  input  in_2,
  input  in_3,
  input  in_4,
  input  in_5,
  input  in_6,
  input  in_7,
  input  in_8,
  output [7:0] out_9
);

  wire multiplexer_1_out, xor_1_out;
  wire [3:0] A0, A1, counter_1_q, H;

  Multiplexer #(.select(2), .disabled(0), .enable("false")) multiplexer_1 (
    .in0(in_1), .in1(in_2), .in2(in_3), .in3(in_4), .out(multiplexer_1_out), .sel(H[1:0]));
  xor xor_1 (xor_1_out, multiplexer_1_out, in_8);
  Counter #(.width(4), .max('hb)) counter_1 (
    .load(in_6), .D(A1), .count(in_7), .Q(counter_1_q), .clk(in_5), .clr(in_4));  // open: carry
  ROM #(.addrWidth(4), .dataWidth(20)) rom_1 (.addr(counter_1_q), .data({out_9, H, A0, A1}));  // open: sel

  // Other names for the same wires on the sheet: CMD[7:0] = out_9; CLK = in_5; P0 = in_2; P1 = in_3; RI = in_1;
  //   RST = in_4

  // Notes on the sheet:
  //   contents of rom_1 (hex, n*v repeats v):
  //   80071 40082 200aa b390 100bb d390 9390 71 82 390 143 265
endmodule

module RG16 (
  input  [15:0] in_1,
  input  in_2,
  input  in_3,
  input  in_4,
  output [15:0] out_5
);

  D_Flip_Flop d_ff_1 (.clk(in_4), .D(in_1[0]), .Q(out_5[0]), .en(in_2), .reset(in_3));  // open: Qn, preset
  D_Flip_Flop d_ff_2 (.clk(in_4), .D(in_1[1]), .Q(out_5[1]), .en(in_2), .reset(in_3));  // open: Qn, preset
  D_Flip_Flop d_ff_3 (.clk(in_4), .D(in_1[0]), .Q(out_5[0]), .en(in_2), .reset(in_3));  // open: Qn, preset
  D_Flip_Flop d_ff_4 (.clk(in_4), .D(in_1[1]), .Q(out_5[1]), .en(in_2), .reset(in_3));  // open: Qn, preset

  // Other names for the same wires on the sheet: CLK = in_4; D[15:0] = in_1; D0 = in_1[0]; D1 = in_1[1]; D2 = in_1[2];
  //   D3 = in_1[3]; D4 = in_1[4]; D5 = in_1[5]; D6 = in_1[6]; D7 = in_1[7]; D8 = in_1[8]; D9 = in_1[9];
  //   D10 = in_1[10]; D11 = in_1[11]; D12 = in_1[12]; D13 = in_1[13]; D14 = in_1[14]; D15 = in_1[15]; E = in_2;
  //   Q[15:0] = out_5; Q0 = out_5[0]; Q1 = out_5[1]; Q2 = out_5[2]; Q3 = out_5[3]; Q4 = out_5[4]; Q5 = out_5[5];
  //   Q6 = out_5[6]; Q7 = out_5[7]; Q8 = out_5[8]; Q9 = out_5[9]; Q10 = out_5[10]; Q11 = out_5[11]; Q12 = out_5[12];
  //   Q13 = out_5[13]; Q14 = out_5[14]; Q15 = out_5[15]; RST = in_3

  // Notes on the sheet:
  //   little-endian storage reg
endmodule

module RGS16 (
  input  [15:0] in_1,
  input  [1:0] in_2,
  input  in_3,
  input  in_4,
  input  in_5,
  input  in_6,
  input  in_7,
  output [15:0] out_8
);

  wire multiplexer_1_out, multiplexer_2_out, multiplexer_3_out, multiplexer_4_out, multiplexer_5_out,
       multiplexer_6_out, multiplexer_7_out, multiplexer_8_out, multiplexer_9_out, multiplexer_10_out,
       multiplexer_11_out, multiplexer_12_out, multiplexer_13_out, multiplexer_14_out, multiplexer_15_out,
       multiplexer_16_out;

  D_Flip_Flop d_ff_1 (.clk(in_7), .D(multiplexer_1_out), .Q(out_8[0]), .en(in_5), .reset(in_6));  // open: Qn, preset
  Multiplexer #(.select(2), .disabled(0), .enable("false")) multiplexer_1 (
    .in0(out_8[0]), .in1(out_8[1]), .in2(in_4), .in3(in_1[0]), .out(multiplexer_1_out), .sel(in_2));
  D_Flip_Flop d_ff_2 (.clk(in_7), .D(multiplexer_2_out), .Q(out_8[1]), .en(in_5), .reset(in_6));  // open: Qn, preset
  Multiplexer #(.select(2), .disabled(0), .enable("false")) multiplexer_2 (
    .in0(out_8[1]), .in1(out_8[2]), .in2(out_8[0]), .in3(in_1[1]), .out(multiplexer_2_out), .sel(in_2));
  D_Flip_Flop d_ff_3 (.clk(in_7), .D(multiplexer_3_out), .Q(out_8[2]), .en(in_5), .reset(in_6));  // open: Qn, preset
  Multiplexer #(.select(2), .disabled(0), .enable("false")) multiplexer_3 (
    .in0(out_8[2]), .in1(out_8[3]), .in2(out_8[1]), .in3(in_1[2]), .out(multiplexer_3_out), .sel(in_2));
  D_Flip_Flop d_ff_4 (.clk(in_7), .D(multiplexer_4_out), .Q(out_8[3]), .en(in_5), .reset(in_6));  // open: Qn, preset
  Multiplexer #(.select(2), .disabled(0), .enable("false")) multiplexer_4 (
    .in0(out_8[3]), .in1(out_8[4]), .in2(out_8[2]), .in3(in_1[3]), .out(multiplexer_4_out), .sel(in_2));
  D_Flip_Flop d_ff_5 (.clk(in_7), .D(multiplexer_5_out), .Q(out_8[4]), .en(in_5), .reset(in_6));  // open: Qn, preset
  Multiplexer #(.select(2), .disabled(0), .enable("false")) multiplexer_5 (
    .in0(out_8[4]), .in1(out_8[5]), .in2(out_8[3]), .in3(in_1[4]), .out(multiplexer_5_out), .sel(in_2));
  D_Flip_Flop d_ff_6 (.clk(in_7), .D(multiplexer_6_out), .Q(out_8[5]), .en(in_5), .reset(in_6));  // open: Qn, preset
  Multiplexer #(.select(2), .disabled(0), .enable("false")) multiplexer_6 (
    .in0(out_8[5]), .in1(out_8[6]), .in2(out_8[4]), .in3(in_1[5]), .out(multiplexer_6_out), .sel(in_2));
  D_Flip_Flop d_ff_7 (.clk(in_7), .D(multiplexer_7_out), .Q(out_8[6]), .en(in_5), .reset(in_6));  // open: Qn, preset
  Multiplexer #(.select(2), .disabled(0), .enable("false")) multiplexer_7 (
    .in0(out_8[6]), .in1(out_8[7]), .in2(out_8[5]), .in3(in_1[6]), .out(multiplexer_7_out), .sel(in_2));
  D_Flip_Flop d_ff_8 (.clk(in_7), .D(multiplexer_8_out), .Q(out_8[7]), .en(in_5), .reset(in_6));  // open: Qn, preset
  Multiplexer #(.select(2), .disabled(0), .enable("false")) multiplexer_8 (
    .in0(out_8[7]), .in1(out_8[8]), .in2(out_8[6]), .in3(in_1[7]), .out(multiplexer_8_out), .sel(in_2));
  D_Flip_Flop d_ff_9 (.clk(in_7), .D(multiplexer_9_out), .Q(out_8[8]), .en(in_5), .reset(in_6));  // open: Qn, preset
  Multiplexer #(.select(2), .disabled(0), .enable("false")) multiplexer_9 (
    .in0(out_8[8]), .in1(out_8[9]), .in2(out_8[7]), .in3(in_1[8]), .out(multiplexer_9_out), .sel(in_2));
  D_Flip_Flop d_ff_10 (.clk(in_7), .D(multiplexer_10_out), .Q(out_8[9]), .en(in_5), .reset(in_6));  // open: Qn, preset
  Multiplexer #(.select(2), .disabled(0), .enable("false")) multiplexer_10 (
    .in0(out_8[9]), .in1(out_8[10]), .in2(out_8[8]), .in3(in_1[9]), .out(multiplexer_10_out), .sel(in_2));
  D_Flip_Flop d_ff_11 (.clk(in_7), .D(multiplexer_11_out), .Q(out_8[10]), .en(in_5), .reset(in_6));  // open: Qn, preset
  Multiplexer #(.select(2), .disabled(0), .enable("false")) multiplexer_11 (
    .in0(out_8[10]), .in1(out_8[11]), .in2(out_8[9]), .in3(in_1[10]), .out(multiplexer_11_out), .sel(in_2));
  D_Flip_Flop d_ff_12 (.clk(in_7), .D(multiplexer_12_out), .Q(out_8[11]), .en(in_5), .reset(in_6));  // open: Qn, preset
  Multiplexer #(.select(2), .disabled(0), .enable("false")) multiplexer_12 (
    .in0(out_8[11]), .in1(out_8[12]), .in2(out_8[10]), .in3(in_1[11]), .out(multiplexer_12_out), .sel(in_2));
  Multiplexer #(.select(2), .disabled(0), .enable("false")) multiplexer_13 (
    .in0(out_8[12]), .in1(out_8[13]), .in2(out_8[11]), .in3(in_1[12]), .out(multiplexer_13_out), .sel(in_2));
  Multiplexer #(.select(2), .disabled(0), .enable("false")) multiplexer_14 (
    .in0(out_8[13]), .in1(out_8[14]), .in2(out_8[12]), .in3(in_1[13]), .out(multiplexer_14_out), .sel(in_2));
  Multiplexer #(.select(2), .disabled(0), .enable("false")) multiplexer_15 (
    .in0(out_8[14]), .in1(out_8[15]), .in2(out_8[13]), .in3(in_1[14]), .out(multiplexer_15_out), .sel(in_2));
  Multiplexer #(.select(2), .disabled(0), .enable("false")) multiplexer_16 (
    .in0(out_8[15]), .in1(in_3), .in2(out_8[14]), .in3(in_1[15]), .out(multiplexer_16_out), .sel(in_2));
  D_Flip_Flop d_ff_13 (.clk(in_7), .D(multiplexer_13_out), .Q(out_8[12]), .en(in_5), .reset(in_6));  // open: Qn, preset
  D_Flip_Flop d_ff_14 (.clk(in_7), .D(multiplexer_14_out), .Q(out_8[13]), .en(in_5), .reset(in_6));  // open: Qn, preset
  D_Flip_Flop d_ff_15 (.clk(in_7), .D(multiplexer_15_out), .Q(out_8[14]), .en(in_5), .reset(in_6));  // open: Qn, preset
  D_Flip_Flop d_ff_16 (.clk(in_7), .D(multiplexer_16_out), .Q(out_8[15]), .en(in_5), .reset(in_6));  // open: Qn, preset

  // Other names for the same wires on the sheet: A[1:0] = in_2; CLK = in_7; D[15:0] = in_1; D0 = in_1[0];
  //   D1 = in_1[1]; D2 = in_1[2]; D3 = in_1[3]; D4 = in_1[4]; D5 = in_1[5]; D6 = in_1[6]; D7 = in_1[7]; D8 = in_1[8];
  //   D9 = in_1[9]; D10 = in_1[10]; D11 = in_1[11]; D12 = in_1[12]; D13 = in_1[13]; D14 = in_1[14]; D15 = in_1[15];
  //   E = in_5; L = in_4; Q[15:0] = out_8; Q0 = out_8[0]; Q1 = out_8[1]; Q2 = out_8[2]; Q3 = out_8[3]; Q4 = out_8[4];
  //   Q5 = out_8[5]; Q6 = out_8[6]; Q7 = out_8[7]; Q8 = out_8[8]; Q9 = out_8[9]; Q10 = out_8[10]; Q11 = out_8[11];
  //   Q12 = out_8[12]; Q13 = out_8[13]; Q14 = out_8[14]; Q15 = out_8[15]; R = in_3; RST = in_6

  // Notes on the sheet:
  //   little-endian shift reg
  //   A1
  //   0
  //   0
  //   1
  //   1
  //   A0
  //   0
  //   1
  //   0
  //   1
  //   результат
  //   хранение
  //   вправо
  //   влево
  //   запись
endmodule

module mega_test_vk (
  input  [1:0] in_1,
  input  in_2,
  input  in_3,
  input  in_4,
  input  in_5,
  input  [15:0] in_6,
  input  [1:0] in_7,
  input  in_8,
  input  in_9,
  input  in_10,
  input  in_11,
  output [15:0] out_12,
  output [15:0] out_13
);

  wire clock_1_out, clock_2_out;
  wire [15:0] adder_1_out;

  Clock clock_1 (.out(clock_1_out));
  Clock clock_2 (.out(clock_2_out));
  RGS16 rgs16_1 (
    .in_1(adder_1_out), .in_2(in_1), .in_3(in_2), .in_4(in_3), .in_5(in_4), .in_6(in_5), .in_7(clock_1_out),
    .out_8(out_12));
  RGS16 rgs16_2 (
    .in_1(in_6), .in_2(in_7), .in_3(in_8), .in_4(in_9), .in_5(in_10), .in_6(in_11), .in_7(clock_2_out),
    .out_8(out_13));
  Adder #(.width(16)) adder_1 (.a(out_12), .b(out_13), .out(adder_1_out));  // open: cin, cout
endmodule

module \ОА  (
  input  [15:0] in_1,
  input  [15:0] in_2,
  input  [15:0] in_3,
  input  RST,
  input  [2:0] WIRE1_CTRL,
  input  in_6,
  input  [2:0] WIRE2_CTRL,
  input  in_8,
  input  [9:0] RG_MODE,
  input  [2:0] KC_MODE,
  input  [1:0] RG_ERR_SET,
  input  ERR_SET,
  input  READY_OUT_SET,
  input  [2:0] ROM_SET,
  input  ENABLE_SET_ROM
);

  wire ADD, adder_1_cout, AND, and_2_out, and_3_out, BRK, button_1_out, CLK, CMP, comparator_1_eq,
       comparator_1_lt, E, ERGS_A, ERGS_B, ERGS_C, ERGS_D, ERGS_E, ERGS_F, ERGS_G, ERGS_H, ERGS_K, EROM, ERR,
       FIN, INP, MOV, multiplexer_6_out, NOT, not_2_out, not_3_out, not_4_out, OR, or_1_out, or_2_out,
       or_3_out, or_6_out, OVERFLOW, P_EQUAL, P_LESS, P_NEQUAL, RI, RO, SHL, SHR, SUB, subtractor_2_bout,
       XOR, xor_2_out;
  wire [1:0] RG_ERR, RG_ERR_SET_t, RGS_MODE;
  wire [2:0] H, KC_MODE_t;
  wire [3:0] CMD, register_2_q, WIRE2_CTRL_t;
  wire [3:2] ROM_SET_t;
  wire [7:0] counter_1_q, S;
  wire [15:0] adder_1_out, and_1_out, controlled_buffer_1_out, KC_RES, not_1_out, or_5_out, RGS_A, RGS_B,
       RGS_C, RGS_D, RGS_E, RGS_F, RGS_G, RGS_H, RGS_K, RMV, subtractor_1_out, subtractor_2_out, WIRE1,
       WIRE2, xor_1_out;

  Decoder #(.select(4), .enable("false")) decoder_1 (
    .out0(CMP), .out1(MOV), .out2(AND), .out3(OR), .out4(NOT), .out5(XOR), .out6(ADD), .out7(SUB),
    .out8(EROM), .out9(INP), .out10(FIN), .out11(ERR), .out12(SHR), .out13(SHL), .out14(BRK), .sel(CMD));  // open: out15
  or or_1 (or_1_out, or_2_out, or_3_out);
  or or_2 (or_2_out, SHR, SHL);
  or or_3 (or_3_out, MOV, INP);
  Decoder #(.select(4), .disabled(0)) decoder_2 (
    .out0(ERGS_A), .out1(ERGS_B), .out2(ERGS_C), .out3(ERGS_D), .out4(ERGS_E), .out5(ERGS_F), .out6(ERGS_G),
    .out7(ERGS_H), .sel({ROM_SET_t, RG_ERR_SET_t}), .en(or_1_out));  // open: out8, out9, out10, out11, out12, out13, out14, out15
  Multiplexer #(.width(2)) multiplexer_1 (.in0(2'b00), .in1(2'b11), .out(RGS_MODE), .sel(or_3_out), .en(or_3_out));
  Multiplexer #(.width(2)) multiplexer_2 (.in0(2'b01), .in1(2'b10), .out(RGS_MODE), .sel(SHL), .en(or_2_out));
  Priority_Encoder #(.disabled(0)) priority_encoder_1 (
    .in0(AND), .in1(OR), .in2(NOT), .in3(XOR), .in4(ADD), .in5(SUB), .out(KC_MODE_t));  // open: in6, in7, en_in, gs, en_out
  or or_4 (ERGS_K, AND, OR, NOT, XOR, ADD, SUB);
  Multiplexer #(.width(2)) multiplexer_3 (.in0(2'b00), .in1(2'b11), .out(RGS_MODE), .sel(ERGS_K), .en(ERGS_K));
  // Probe on RG_ERR
  Register #(.width(2)) register_1 (.D(RG_ERR_SET_t), .en(ERR), .Q(RG_ERR), .clk(CLK), .clr(RST));
  D_Flip_Flop d_ff_1 (.clk(CLK), .D(1'b1), .Q(RO), .en(FIN), .reset(RST));  // open: Qn, preset
  // Probe on {ROM_SET_t, RG_ERR_SET_t}
  Register #(.width(4)) register_2 (.D({ROM_SET_t, RG_ERR_SET_t}), .en(EROM), .Q(register_2_q), .clk(CLK), .clr(RST));
  // Probe on RGS_A
  RGS16 rgs16_1 (
    .in_1(WIRE2), .in_2(RGS_MODE), .in_3(1'b0), .in_4(1'b0), .in_5(ERGS_A), .in_6(RST), .in_7(CLK),
    .out_8(RGS_A));
  // Probe on WIRE1
  Multiplexer #(.select(4), .width(16), .disabled(0), .enable("false")) multiplexer_4 (
    .in0(RGS_A), .in1(RGS_B), .in2(RGS_C), .in3(RGS_D), .in4(RGS_E), .in5(RGS_F), .in6(RGS_G), .in7(RGS_H),
    .in13(RGS_K), .in14(RMV), .in15(WIRE2), .out(WIRE1), .sel({ROM_SET_t, RG_ERR_SET_t}));  // open: in8, in9, in10, in11, in12
  // Probe on {ROM_SET_t, RG_ERR_SET_t}
  // Probe on WIRE2
  Multiplexer #(.select(4), .width(16), .disabled(0), .enable("false")) multiplexer_5 (
    .in0(RGS_A), .in1(RGS_B), .in2(RGS_C), .in3(RGS_D), .in4(RGS_E), .in5(RGS_F), .in6(RGS_G), .in7(RGS_H),
    .in13(RGS_K), .in14(RMV), .in15(in_3), .out(WIRE2), .sel(WIRE2_CTRL_t));  // open: in8, in9, in10, in11, in12
  // Probe on WIRE2_CTRL_t
  // Probe on RMV
  ROM #(.addrWidth(4), .dataWidth(16)) rom_1 (.addr(register_2_q), .data(RMV));  // open: sel
  // Probe on RGS_B
  RGS16 rgs16_2 (
    .in_1(WIRE2), .in_2(RGS_MODE), .in_3(1'b0), .in_4(1'b0), .in_5(ERGS_B), .in_6(RST), .in_7(CLK),
    .out_8(RGS_B));
  Button button_1 (.out(button_1_out));
  filter filter_1 (.in_1(CLK), .in_2(button_1_out), .in_3(1'b1), .out_5(RI));  // open: out_4
  Subtractor #(.width(16)) subtractor_1 (.a(in_1), .b(in_2), .out(subtractor_1_out));  // open: bin, bout
  assign and_1_out = WIRE1 & WIRE2;  // AND_Gate and_1, 16 bits wide
  assign or_5_out = WIRE1 | WIRE2;  // OR_Gate or_5, 16 bits wide
  assign not_1_out = ~WIRE1;  // NOT_Gate not_1, 16 bits wide
  assign xor_1_out = WIRE1 ^ WIRE2;  // XOR_Gate xor_1, 16 bits wide
  Adder #(.width(16)) adder_1 (.a(WIRE1), .b(WIRE2), .out(adder_1_out), .cout(adder_1_cout));  // open: cin
  Subtractor #(.width(16)) subtractor_2 (
    .a(WIRE1), .b(WIRE2), .out(subtractor_2_out), .bout(subtractor_2_bout));  // open: bin
  // Probe on subtractor_1_out
  // Probe on RGS_C
  RGS16 rgs16_3 (
    .in_1(WIRE2), .in_2(RGS_MODE), .in_3(1'b0), .in_4(1'b0), .in_5(ERGS_C), .in_6(RST), .in_7(CLK),
    .out_8(RGS_C));
  and and_2 (and_2_out, adder_1_cout, ~KC_MODE_t[0], ~KC_MODE_t[1], KC_MODE_t[2]);  // AND_Gate
  and and_3 (and_3_out, subtractor_2_bout, KC_MODE_t[0], ~KC_MODE_t[1], KC_MODE_t[2]);  // AND_Gate
  or or_6 (or_6_out, and_2_out, and_3_out);
  Multiplexer #(.select(3), .disabled(0), .enable("false")) multiplexer_6 (
    .in0(1'b0), .in1(RI), .in2(P_NEQUAL), .in3(P_EQUAL), .in4(P_LESS), .in5(OVERFLOW), .in6(in_8),
    .out(multiplexer_6_out), .sel(H));  // open: in7
  // Probe on in_3
  Clock clock_1 (.out(CLK));
  // Probe on KC_RES
  Multiplexer #(.select(3), .width(16), .disabled(0), .enable("false")) multiplexer_7 (
    .in0(and_1_out), .in1(or_5_out), .in2(not_1_out), .in3(xor_1_out), .in4(adder_1_out),
    .in5(subtractor_2_out), .out(KC_RES), .sel(KC_MODE_t));  // open: in6, in7
  D_Flip_Flop d_ff_2 (.clk(CLK), .D(or_6_out), .Q(OVERFLOW), .reset(RST));  // open: Qn, preset, en
  xor xor_2 (xor_2_out, multiplexer_6_out, E);
  // Probe on RGS_D
  RGS16 rgs16_4 (
    .in_1(WIRE2), .in_2(RGS_MODE), .in_3(1'b0), .in_4(1'b0), .in_5(ERGS_D), .in_6(RST), .in_7(CLK),
    .out_8(RGS_D));
  not not_2 (not_2_out, xor_2_out);
  Counter counter_1 (.load(xor_2_out), .D(S), .count(not_2_out), .Q(counter_1_q), .clk(CLK), .clr(RST));  // open: carry
  LED led_1 (.in(CMP));
  LED led_2 (.in(MOV));
  LED led_3 (.in(AND));
  LED led_4 (.in(OR));
  LED led_5 (.in(NOT));
  LED led_6 (.in(XOR));
  LED led_7 (.in(ADD));
  LED led_8 (.in(SUB));
  LED led_9 (.in(EROM));
  LED led_10 (.in(INP));
  LED led_11 (.in(FIN));
  LED led_12 (.in(ERR));
  LED led_13 (.in(SHR));
  LED led_14 (.in(SHL));
  LED led_15 (.in(BRK));
  not not_3 (not_3_out, comparator_1_eq);
  Comparator #(.width(16)) comparator_1 (.a(WIRE1), .b(WIRE2), .eq(comparator_1_eq), .lt(comparator_1_lt));  // open: gt
  RGS16 rgs16_5 (
    .in_1(WIRE2), .in_2(RGS_MODE), .in_3(1'b0), .in_4(1'b0), .in_5(ERGS_E), .in_6(RST), .in_7(CLK),
    .out_8(RGS_E));
  RGS16 rgs16_6 (
    .in_1(KC_RES), .in_2(RGS_MODE), .in_3(1'b0), .in_4(1'b0), .in_5(ERGS_K), .in_6(RST), .in_7(CLK),
    .out_8(RGS_K));
  D_Flip_Flop d_ff_3 (.clk(CLK), .D(not_3_out), .Q(P_NEQUAL), .en(CMP), .reset(RST));  // open: Qn, preset
  D_Flip_Flop d_ff_4 (.clk(CLK), .D(comparator_1_eq), .Q(P_EQUAL), .en(CMP), .reset(RST));  // open: Qn, preset
  D_Flip_Flop d_ff_5 (.clk(CLK), .D(comparator_1_lt), .Q(P_LESS), .en(CMP), .reset(RST));  // open: Qn, preset
  ROM #(.dataWidth(24)) rom_2 (
    .addr(counter_1_q), .data({CMD, ROM_SET_t, RG_ERR_SET_t, WIRE2_CTRL_t, H, E, S}));  // open: sel
  // Probe on {ROM_SET_t, RG_ERR_SET_t}
  // Probe on WIRE2_CTRL_t
  // Probe on RG_ERR
  LED led_16 (.in(RO));
  // Probe on controlled_buffer_1_out
  assign controlled_buffer_1_out = RO ? RGS_A : 16'bz;  // Controlled_Buffer controlled_buffer_1
  // Probe on controlled_buffer_1_out
  // Probe on RGS_E
  // Probe on RGS_K
  // Probe on RGS_F
  RGS16 rgs16_7 (
    .in_1(WIRE2), .in_2(RGS_MODE), .in_3(1'b0), .in_4(1'b0), .in_5(ERGS_F), .in_6(RST), .in_7(CLK),
    .out_8(RGS_F));
  // Probe on RGS_G
  RGS16 rgs16_8 (
    .in_1(WIRE2), .in_2(RGS_MODE), .in_3(1'b0), .in_4(1'b0), .in_5(ERGS_G), .in_6(RST), .in_7(CLK),
    .out_8(RGS_G));
  not not_4 (not_4_out, not_4_out);

  // Other names for the same wires on the sheet: ROM_SET_t[1:0] = RG_ERR_SET_t;
  //   WIRE1_CTRL_t[3:0] = {ROM_SET_t, RG_ERR_SET_t}; BREAKPOINT = in_8; ERR_SET_t = ERR; INPUT[15:0] = in_3;
  //   RO_SET = FIN; ROM = EROM

  // Notes on the sheet:
  //   RGS_A
  //   contents of rom_1 (hex, n*v repeats v):
  //   0 1 8000 7c00 3ff 7fff a b f 400 ffe0 800 ffff 20
  //   RGS_B
  //   RGS_C
  //   CLK
  //   RGS_D
  //   RGS_E
  //   RGS_K
  //   contents of rom_2 (hex, n*v repeats v):
  //   90f300 830001 20e002 de003 40f 840005 20e006 800007 de008 40d 83000a 10e00b a0010c b1000d a0010e
  //   83000f 20e010 11d011 840012 20e013 12d014 800015 1e016 61b 890018 32e019 12d01a 13201b 14201c 80001d
  //   12e01e 11e01f 800020 4e021 639 810023 24e024 de025 628 133 623028 12d029 133 81002b 22e02c 15d02d
  //   c2002e c3002f 810030 61e031 11d032 8b0033 e3034 82b d30036 c40037 120 8b0039 22e03a de03b 447 81003d
  //   22e03e 15e03f 625040 12d041 810042 61e043 11d044 c20045 149 625047 12d048 830049 20e04a 13d04b
  //   86004c 15e04d 80004e 5e04f 656 c30051 810052 75e053 15d054 14e 633056 13d057 880058 73e059 13d05a
  //   63105b 13d05c 86005d 73e05e 13d05f 820060 23e061 de062 67d 8d0064 22e065 ed066 60a 800068 15e069
  //   86006a 15e06b 80006c 5e06d 674 d3006f 810070 75e071 15d072 16c 175 840075 22e076 12d077 800078
  //   10e079 33207a 10d07b a0017c e00d7d 81007e 22e07f de080 c20081 485 62e083 12d084 800085 3e086 675
  //   c20088 810089 63e08a 13d08b 22e08c de08d 685 62e08f 12d090 185
  //   RGS_F
  //   RGS_G
endmodule

module \деление  (
  input  [3:0] in_1
);

  wire clock_1_out;
  wire [3:0] adder_1_out, multiplexer_1_out, not_1_out;
  wire [4:0] register_1_q;

  // Probe on in_1
  assign not_1_out = ~in_1;  // NOT_Gate not_1, 4 bits wide
  Adder #(.width(4)) adder_1 (.a(not_1_out), .b(4'b0001), .out(adder_1_out));  // open: cin, cout
  Multiplexer #(.width(4), .enable("false")) multiplexer_1 (
    .in0(in_1), .in1(adder_1_out), .out(multiplexer_1_out), .sel(in_1[3]));
  Register #(.width(5)) register_1 (
    .D({1'b0, multiplexer_1_out}), .Q(register_1_q), .clk(clock_1_out));  // open: en, clr
  Clock clock_1 (.out(clock_1_out));
  // Probe on register_1_q
endmodule
